# Fritzing sketch Joystick_Fritzing (saved by Fritzing 0.9.3b)

parts:
  Composant1 = NRF24L01+ Breakout Board
  TP1 = TP4056 [chip_label=TP4056 package="DIP (Dual Inline) [THT]"]
  U2 = DC-DC 2-24V Step Up Booster [package=THT]
  S2 = Toggle Switch [package=THT]
  M3 = DOIT Esp32 DevKit v1 (30 pins long, 11 pins width) [part_number=ESP32S-PIN30]
  U3 = BATTERY-2 [package=battery-aa]
  Composant2 = Thumb Joystick
  S3 = Pushbutton [package="[THT]"]
  S4 = Pushbutton [package="[THT]"]
  S5 = Pushbutton [package="[THT]"]
  S6 = Pushbutton [package="[THT]"]

nets:
  GND: Composant1.GND, U2.pin2, M3.GND, Composant2.GND, S3.Pin_1, S3.Pin_2, S4.Pin_1, S4.Pin_2, S5.Pin_1, S5.Pin_2, S6.Pin_1, S6.Pin_2
  VCC: Composant1.VCC, M3.3V3
  N1: Composant1.CE, M3.D5
  N2: Composant1.CS, M3.TX2
  N3: Composant1.SCK, M3.D18
  N4: Composant1.MOSI, M3.D23
  N5: Composant1.MISO, M3.D19
  N6: TP1.pin3, S2.L1
  N7: TP1.pin4, U3.+1
  N8: TP1.pin5, U3.-1
  N9: TP1.pin6, U2.pin3
  N10: U2.pin1, M3.VIN
  N11: U2.pin4, S2.COM
  N12: M3.D33, S5.Pin_3, S5.Pin_4
  N13: M3.D25, S3.Pin_3, S3.Pin_4
  N14: M3.D26, S4.Pin_3, S4.Pin_4
  N15: M3.D27, S6.Pin_3, S6.Pin_4
  N16: M3.D14, Composant2.SEL
  N17: M3.D12, Composant2.HORZ
  N18: M3.D13, Composant2.VERT

custom parts:
  TP4056: A DIP stand-in part for whatever IC you want. With 6 pins on a 300mil dual inline package (DIP) footprint.
  DC-DC 2-24V Step Up Booster: Convertisseur DC-DC 2-24V 2A
  DOIT Esp32 DevKit v1 (30 pins long, 11 pins width): The DOIT Esp32 DevKit v1 is one of the development board created by DOIT to evaluate the ESP-WROOM-32 module. It is based on the ESP32 microcontroller that boasts Wifi, Bluetooth, Ethernet and Low Power support all in a single chip. (vanepp) made breadboard work, adjusted pin numbering and labels and reduced size of schematic and cleaned up pcb. This chip is 30pins long (2 x15) and 11 pins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
