# Fritzing sketch Robot_Fritzing (saved by Fritzing 0.9.3b)

parts:
  Composant1 = NRF24L01+ Breakout Board
  TP1 = TP4056 [chip_label=TP4056 package="DIP (Dual Inline) [THT]"]
  U2 = DC-DC 2-24V Step Up Booster [package=THT]
  M1 = DC Motor  # not connected
  M2 = DC Motor  # not connected
  S2 = Toggle Switch [package=THT]
  VCC1 = Battery  # not connected
  M3 = DOIT Esp32 DevKit v1 (30 pins long, 11 pins width) [part_number=ESP32S-PIN30]
  S3 = H-Bridge with L298N

nets:
  GND: Composant1.GND, U2.pin2, M3.GND, S3.GND
  VCC: Composant1.VCC, M3.3V3
  N1: Composant1.CE, M3.D5
  N2: Composant1.CS, M3.TX2
  N3: Composant1.SCK, M3.D18
  N4: Composant1.MOSI, M3.D23
  N5: Composant1.MISO, M3.D19
  N6: TP1.pin3, S2.L1
  N7: TP1.pin6, U2.pin3
  N8: U2.pin1, S3.12V
  N9: U2.pin4, S2.COM
  N10: M3.D25, S3.ENB
  N11: M3.D26, S3.ENA
  N12: M3.D27, S3.IN4
  N13: M3.D14, S3.IN3
  N14: M3.D12, S3.IN2
  N15: M3.D13, S3.IN1
  VIN: M3.VIN, S3.5V

custom parts:
  TP4056: A DIP stand-in part for whatever IC you want. With 6 pins on a 300mil dual inline package (DIP) footprint.
  DC-DC 2-24V Step Up Booster: Convertisseur DC-DC 2-24V 2A
  Battery: Your standard 2x 18650 battery pack (7,4 Volts)
  DOIT Esp32 DevKit v1 (30 pins long, 11 pins width): The DOIT Esp32 DevKit v1 is one of the development board created by DOIT to evaluate the ESP-WROOM-32 module. It is based on the ESP32 microcontroller that boasts Wifi, Bluetooth, Ethernet and Low Power support all in a single chip. (vanepp) made breadboard work, adjusted pin numbering and labels and reduced size of schematic and cleaned up pcb. This chip is 30pins long (2 x15) and 11 pins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
  H-Bridge with L298N: h-bridge
